// Logisim project memselect.circ as structural Verilog: 1 circuit, main circuit main
module main (
  input  _15,
  input  _14,
  input  _13,
  input  _12,
  input  RESET,
  input  ADDR15
);

  wire and_1_out, nand_1_out, nor_1_out, nor_2_out, not_1_out;

  nor nor_1 (nor_1_out, RESET, nor_2_out);
  nor nor_2 (nor_2_out, nor_1_out, ADDR15);
  nand nand_1 (nand_1_out, _15, _14, _13, _12);
  and and_1 (and_1_out, nand_1_out, nor_1_out);
  not not_1 (not_1_out, and_1_out);
  // Probe on and_1_out
  // Probe on not_1_out

  // Notes on the sheet:
  //   select jumper hi or out of sr
  //   possible need to gate with rd wr
endmodule
