// Logisim project test4.circ as structural Verilog: 1 circuit, main circuit Register File
module Register_File (
  input  RESET,
  input  RUN,
  input  in_3
);

  wire clk_out, clock_1_out, COND1, COND2, COND3, DNZ, DZ, LD_BR, LD_INS, MEM_IN, MEM_OUT, MEM_RD, MEM_WR,
       multiplexer_1_out, not_1_out, not_2_out, or_1_out, PC_INC, PC_LD, PC_OUT, PCLDR, R0_AOUT, R0_DIN,
       R0_DOUT, R1_AOUT, R1_DIN, R1_DOUT, R2_AOUT, R2_DIN, R2_DOUT, R3_AOUT, R3_DIN, R3_DOUT, R_CT, R_LD,
       RST_UC;
  wire [4:0] uCode_PC_q;
  wire [7:0] Addr, BData, controlled_buffer_12_out, counter_1_q, counter_2_q, counter_3_q, counter_4_q,
       counter_5_q, counter_6_q, Data, Inst_Reg_q, ram_1_data, rom_2_data;
  wire [25:3] rom_1_data;

  not not_1 (not_1_out, PCLDR);
  Multiplexer #(.select(3), .disabled(0), .enable("false")) multiplexer_1 (
    .in0(1'b1), .in1(DZ), .in2(DNZ), .in3(1'b0), .in4(1'b0), .in5(1'b0), .in6(1'b0), .in7(1'b0),
    .out(multiplexer_1_out), .sel({COND3, COND2, COND1}));
  Counter counter_1 (.load(R_LD), .D(Data), .count(R_CT), .Q(counter_1_q), .clk(R0_DIN), .clr(RESET));  // open: carry
  Counter counter_2 (.load(R_LD), .D(Data), .count(R_CT), .Q(counter_2_q), .clk(R1_DIN), .clr(RESET));  // open: carry
  Counter counter_3 (.load(R_LD), .D(Data), .count(R_CT), .Q(counter_3_q), .clk(R2_DIN), .clr(RESET));  // open: carry
  Counter counter_4 (.load(R_LD), .D(Data), .count(R_CT), .Q(counter_4_q), .clk(R3_DIN), .clr(RESET));  // open: carry
  assign Addr = PC_OUT ? counter_5_q : 8'bz;  // Controlled_Buffer controlled_buffer_1
  Counter counter_5 (
    .load(PCLDR), .D(BData), .count(not_1_out), .Q(counter_5_q), .clk(PC_INC), .clr(RESET));  // open: carry
  RAM #(.bus("asynch")) ram_1 (.addr(Addr), .data(ram_1_data), .sel(1'b1), .ld(not_2_out), .clr(1'b0));
  not not_2 (not_2_out, MEM_WR);
  and and_1 (PCLDR, PC_LD, multiplexer_1_out);
  assign Data = R0_DOUT ? counter_1_q : 8'bz;  // Controlled_Buffer controlled_buffer_2
  assign Addr = R0_AOUT ? counter_1_q : 8'bz;  // Controlled_Buffer controlled_buffer_3
  assign Data = R1_DOUT ? counter_2_q : 8'bz;  // Controlled_Buffer controlled_buffer_4
  assign Addr = R1_AOUT ? counter_2_q : 8'bz;  // Controlled_Buffer controlled_buffer_5
  assign Data = R2_DOUT ? counter_3_q : 8'bz;  // Controlled_Buffer controlled_buffer_6
  assign Addr = R2_AOUT ? counter_3_q : 8'bz;  // Controlled_Buffer controlled_buffer_7
  assign Data = R3_DOUT ? counter_4_q : 8'bz;  // Controlled_Buffer controlled_buffer_8
  assign Addr = R3_AOUT ? counter_4_q : 8'bz;  // Controlled_Buffer controlled_buffer_9
  // Probe on Addr
  assign Data = MEM_OUT ? ram_1_data : 8'bz;  // Controlled_Buffer controlled_buffer_10
  assign ram_1_data = MEM_IN ? Data : 8'bz;  // Controlled_Buffer controlled_buffer_11
  // Probe on Data
  Register Branch_Register (.D(Data), .en(RUN), .Q(BData), .clk(LD_BR), .clr(RESET));
  Clock clk (.out(clk_out));
  Counter #(.width(5), .max('h1f)) uCode_PC (
    .load(1'b0), .count(RUN), .Q(uCode_PC_q), .clk(clk_out), .clr(or_1_out));  // open: D, carry
  or or_1 (or_1_out, RESET, RST_UC);
  Clock clock_1 (.out(clock_1_out));
  not not_3 (R_LD, rom_1_data[25]);
  // Probe on uCode_PC_q
  Counter counter_6 (.Q(counter_6_q), .clk(clock_1_out));  // open: load, D, count, carry, clr
  // Probe on Inst_Reg_q
  Register Inst_Reg (.D(Data), .en(RUN), .Q(Inst_Reg_q), .clk(LD_INS), .clr(RESET));
  assign controlled_buffer_12_out = in_3 ? counter_6_q : 8'bz;  // Controlled_Buffer controlled_buffer_12
  ROM #(.addrWidth(13), .dataWidth(32)) rom_1 (
    .addr({Inst_Reg_q, uCode_PC_q}),
    .data({RST_UC, LD_INS, COND3, COND2, COND1, R_CT, rom_1_data[25], LD_BR, rom_1_data[23], PC_INC, PC_LD, PC_OUT, MEM_RD, MEM_WR, MEM_OUT, MEM_IN, rom_1_data[15], R3_DIN, R3_AOUT, R3_DOUT, rom_1_data[11], R2_DIN, R2_AOUT, R2_DOUT, rom_1_data[7], R1_DIN, R1_AOUT, R1_DOUT, rom_1_data[3], R0_DIN, R0_AOUT, R0_DOUT}),
    .sel(1'b1));
  // Probe on Inst_Reg_q
  ROM rom_2 (.addr(controlled_buffer_12_out), .data(rom_2_data));  // open: sel
  or or_2 (DNZ, Data[0], Data[1], Data[2], Data[3], Data[4], Data[5], Data[6], Data[7]);
  not not_4 (DZ, DNZ);
  Pull_Resistor #(.pull(1)) pull_resistor_1 (.node(RESET));
  assign Data = in_3 ? rom_2_data : 8'bz;  // Controlled_Buffer controlled_buffer_13

  // Other names for the same wires on the sheet: LOAD = in_3

  // Notes on the sheet:
  //   Branch Selector
  //   contents of rom_1 (hex, n*v repeats v):
  //   1a0000 401a0000 30*0 1a0000 401a0000 1 41 400000 80000000 1178*0 1a0000 401a0000 10210 50210 210
  //   400000 80000000 825*0 1a0000 401a0000 400000 1a0000 1a0004 100000 400000 80000000 56*0 1a0000
  //   401a0000 400000 1a0000 1a0400 100000 400000 80000000 56*0 1a0000 401a0000 6000000 6000004 400000
  //   80000000 122*0 1a0000 401a0000 4000000 4000004 400000 80000000 1786*0 1a0000 401a0000 400000 1a0000
  //   10a0000 200000 600000 80000000
endmodule
