// Logisim project test5.circ as structural Verilog: 1 circuit, main circuit Register File
module Register_File (
  input  RESET,
  input  RUN,
  input  LOAD
);

  wire clk_out, COND1, COND2, COND3, DNZ, DZ, IO1, IOADDR, IOR, IOW, LD_BR, LD_CLK_out, LD_INS, LD_WR,
       MEM_IN, MEM_OUT, MEM_RD, MEM_WR, multiplexer_1_out, not_1_out, not_2_out, not_3_out, not_6_out,
       not_7_out, or_2_out, or_3_out, or_4_out, or_5_out, PC_INC, PC_LD, PC_OUT, PCLDR, R0_AOUT, R0_DIN,
       R0_DOUT, R1_AOUT, R1_DIN, R1_DOUT, R2_AOUT, R2_DIN, R2_DOUT, R3_AOUT, R3_DIN, R3_DOUT, R_CT, R_LD,
       RST_UC;
  wire [2:0] IO_Address_q;
  wire [3:0] register_1_q, register_1_q_2;
  wire [4:0] uCode_PC_q;
  wire [7:0] Addr, BData, counter_1_q, counter_2_q, counter_3_q, counter_4_q, counter_5_q, Data, Inst_Reg_q,
       ram_1_data, rom_2_data;
  wire [7:3] IO_Address_q_2;
  wire [9:0] counter_6_q;
  wire [25:11] rom_1_data;

  Counter counter_1 (
    .load(PCLDR), .D(BData), .count(not_1_out), .Q(counter_1_q), .clk(PC_INC), .clr(RESET));  // open: carry
  not not_1 (not_1_out, PCLDR);
  not not_2 (not_2_out, 1'b0);
  assign Data = R0_DOUT ? counter_2_q : 8'bz;  // Controlled_Buffer controlled_buffer_1
  Counter counter_2 (.load(R_LD), .D(Data), .count(R_CT), .Q(counter_2_q), .clk(R0_DIN), .clr(RESET));  // open: carry
  assign Addr = R0_AOUT ? counter_2_q : 8'bz;  // Controlled_Buffer controlled_buffer_2
  assign Data = R1_DOUT ? counter_3_q : 8'bz;  // Controlled_Buffer controlled_buffer_3
  Counter counter_3 (.load(R_LD), .D(Data), .count(R_CT), .Q(counter_3_q), .clk(R1_DIN), .clr(RESET));  // open: carry
  assign Addr = R1_AOUT ? counter_3_q : 8'bz;  // Controlled_Buffer controlled_buffer_4
  assign Data = R2_DOUT ? counter_4_q : 8'bz;  // Controlled_Buffer controlled_buffer_5
  Counter counter_4 (.load(R_LD), .D(Data), .count(R_CT), .Q(counter_4_q), .clk(R2_DIN), .clr(RESET));  // open: carry
  assign Addr = R2_AOUT ? counter_4_q : 8'bz;  // Controlled_Buffer controlled_buffer_6
  assign Data = R3_DOUT ? counter_5_q : 8'bz;  // Controlled_Buffer controlled_buffer_7
  Counter counter_5 (.load(R_LD), .D(Data), .count(R_CT), .Q(counter_5_q), .clk(R3_DIN), .clr(RESET));  // open: carry
  assign Addr = R3_AOUT ? counter_5_q : 8'bz;  // Controlled_Buffer controlled_buffer_8
  assign Addr = PC_OUT ? counter_1_q : 8'bz;  // Controlled_Buffer controlled_buffer_9
  RAM #(.bus("asynch")) ram_1 (.addr(Addr), .data(ram_1_data), .sel(not_2_out), .ld(not_3_out), .clr(1'b0));
  not not_3 (not_3_out, or_3_out);
  and and_1 (PCLDR, PC_LD, multiplexer_1_out);
  Multiplexer #(.select(3), .disabled(0), .enable("false")) multiplexer_1 (
    .in0(1'b1), .in1(DZ), .in2(DNZ), .in3(1'b0), .in4(1'b0), .in5(1'b0), .in6(1'b0), .in7(1'b0),
    .out(multiplexer_1_out), .sel({COND3, COND2, COND1}));
  or or_1 (DNZ, Data[0], Data[1], Data[2], Data[3], Data[4], Data[5], Data[6], Data[7]);
  not not_4 (DZ, DNZ);
  assign Data = MEM_OUT ? ram_1_data : 8'bz;  // Controlled_Buffer controlled_buffer_10
  or or_2 (or_2_out, MEM_IN, LOAD);
  assign ram_1_data = or_2_out ? Data : 8'bz;  // Controlled_Buffer controlled_buffer_11
  or or_3 (or_3_out, MEM_WR, LD_WR);
  Clock clk (.out(clk_out));
  Register Branch_Register (.D(Data), .en(RUN), .Q(BData), .clk(LD_BR), .clr(RESET));
  Counter #(.width(5), .max('h1f)) uCode_PC (
    .load(1'b0), .count(RUN), .Q(uCode_PC_q), .clk(clk_out), .clr(or_4_out));  // open: D, carry
  or or_4 (or_4_out, RESET, RST_UC);
  not not_5 (R_LD, rom_1_data[25]);
  // Probe on uCode_PC_q
  Clock LD_CLK (.out(LD_CLK_out));
  // Probe on Inst_Reg_q
  Register Inst_Reg (.D(Data), .en(RUN), .Q(Inst_Reg_q), .clk(LD_INS), .clr(RESET));
  Counter #(.width(10), .max('h3ff)) counter_6 (
    .Q(counter_6_q), .clk(LD_CLK_out), .clr(or_5_out));  // open: load, D, count, carry
  or or_5 (or_5_out, RESET, not_6_out);
  not not_6 (not_6_out, LOAD);
  ROM #(.addrWidth(13), .dataWidth(32)) rom_1 (
    .addr({Inst_Reg_q, uCode_PC_q}),
    .data({RST_UC, LD_INS, COND3, COND2, COND1, R_CT, rom_1_data[25], LD_BR, rom_1_data[23], PC_INC, PC_LD, PC_OUT, MEM_RD, MEM_WR, MEM_OUT, MEM_IN, IOADDR, R3_DIN, R3_AOUT, R3_DOUT, rom_1_data[11], R2_DIN, R2_AOUT, R2_DOUT, IOW, R1_DIN, R1_AOUT, R1_DOUT, IOR, R0_DIN, R0_AOUT, R0_DOUT}),
    .sel(1'b1));
  // Probe on Inst_Reg_q
  not not_7 (not_7_out, counter_6_q[0]);
  assign Addr = LOAD ? counter_6_q[9:2] : 8'bz;  // Controlled_Buffer controlled_buffer_12
  and and_2 (LD_WR, not_7_out, counter_6_q[1], LOAD);
  Register IO_Address (.D(Data), .en(RUN), .Q({IO_Address_q_2, IO_Address_q}), .clk(IOADDR), .clr(RESET));
  Pull_Resistor #(.pull(1)) pull_resistor_1 (.node(RESET));
  assign Data = LOAD ? rom_2_data : 8'bz;  // Controlled_Buffer controlled_buffer_13
  ROM rom_2 (.addr(Addr), .data(rom_2_data), .sel(LOAD));
  Hex_Digit_Display hex_digit_display_1 (.value(register_1_q_2));  // open: dp
  Register register_1 (.D(Data), .en(IO1), .Q({register_1_q_2, register_1_q}), .clk(IOW), .clr(RESET));
  Decoder #(.select(3), .enable("false")) decoder_1 (
    .out1(IO1), .sel(IO_Address_q));  // open: out0, out2, out3, out4, out5, out6, out7
  Hex_Digit_Display hex_digit_display_2 (.value(register_1_q));  // open: dp

  // Notes on the sheet:
  //   PC
  //   RAM
  //   DATA BUS CONDITIONS
  //   REGISTER FILE
  //   BRANCH SELECTOR
  //   contents of rom_1 (hex, n*v repeats v):
  //   0 1a0000 401a0000 29*0 1a0000 401a0000 1 41 400000 80000000 1178*0 1a0000 401a0000 10210 50210 210
  //   400000 80000000 825*0 1a0000 401a0000 400000 1a0000 1a0004 100000 400000 80000000 56*0 1a0000
  //   401a0000 400000 1a0000 1a0400 100000 400000 80000000 1912*0 1a0000 401a0000 400000 1a0000 1a8000
  //   a0200 a0280 80000000 56*0 1a0000 401a0000 400000 1a0000 10a0000 200000 600000 80000000 2040*0 1a0000
  //   401a0000 6000000 6000004 400000 80000000 122*0 1a0000 401a0000 4000000 4000004 400000 80000000
  //   RAM LOADER
  //   CONTROL
  //   contents of rom_2 (hex, n*v repeats v):
  //   40 55 42 b 1 26 7e 1 c0 80 4
endmodule
