// Logisim project test6.circ as structural Verilog: 1 circuit, main circuit Register File
module Register_File (
  input  RESET,
  input  RUN,
  input  LOAD
);

  wire AC_IN, AC_OUT, AC_WR, ANZ, AZ, clk_out, COND0, COND1, COND2, DNZ, DZ, EQ, GT, IO1, IO2, IO3, IO4, IO5,
       IO6, IO7, IOADDR, IOR, IOW, LD_BR, LD_CLK_out, LD_INS, LD_WR, LT, MEM_IN, MEM_OUT, MEM_RD, MEM_WR,
       multiplexer_1_out, not_1_out, not_2_out, not_3_out, not_7_out, not_8_out, or_2_out, or_3_out,
       or_4_out, or_6_out, PC_AOUT, PC_DOUT, PC_INC, PC_LD, PCLDR, R0_AOUT, R0_DIN, R0_DOUT, R1_AOUT, R1_DIN,
       R1_DOUT, R2_AOUT, R2_DIN, R2_DOUT, R3_AOUT, R3_DIN, R3_DOUT, R_CT, R_LD, RST_UC, SP_AOUT, SP_DIN;
  wire [3:0] ALUSEL, register_2_q, register_2_q_2;
  wire [4:0] uCode_PC_q;
  wire [7:0] adder_1_out, Addr, and_3_out, BData, controlled_buffer_15_out, counter_1_q, counter_2_q,
       counter_3_q, counter_4_q, counter_5_q, counter_6_q, Data, Inst_Reg_q, IO_Address_q, not_9_out,
       or_7_out, ram_1_data, register_1_q, rom_3_data, xor_1_out;
  wire [7:7] rom_2_data;
  wire [9:0] counter_7_q;
  wire [23:23] rom_1_data;

  Counter counter_1 (
    .load(PCLDR), .D(BData), .count(not_1_out), .Q(counter_1_q), .clk(PC_INC), .clr(RESET));  // open: carry
  not not_1 (not_1_out, PCLDR);
  not not_2 (not_2_out, 1'b0);
  assign Data = R0_DOUT ? counter_2_q : 8'bz;  // Controlled_Buffer controlled_buffer_1
  Counter counter_2 (.load(R_LD), .D(Data), .count(R_CT), .Q(counter_2_q), .clk(R0_DIN), .clr(RESET));  // open: carry
  assign Addr = R0_AOUT ? counter_2_q : 8'bz;  // Controlled_Buffer controlled_buffer_2
  assign Data = R1_DOUT ? counter_3_q : 8'bz;  // Controlled_Buffer controlled_buffer_3
  Counter counter_3 (.load(R_LD), .D(Data), .count(R_CT), .Q(counter_3_q), .clk(R1_DIN), .clr(RESET));  // open: carry
  assign Addr = R1_AOUT ? counter_3_q : 8'bz;  // Controlled_Buffer controlled_buffer_4
  assign Data = R2_DOUT ? counter_4_q : 8'bz;  // Controlled_Buffer controlled_buffer_5
  Counter counter_4 (.load(R_LD), .D(Data), .count(R_CT), .Q(counter_4_q), .clk(R2_DIN), .clr(RESET));  // open: carry
  assign Addr = R2_AOUT ? counter_4_q : 8'bz;  // Controlled_Buffer controlled_buffer_6
  assign Data = R3_DOUT ? counter_5_q : 8'bz;  // Controlled_Buffer controlled_buffer_7
  Counter counter_5 (.load(R_LD), .D(Data), .count(R_CT), .Q(counter_5_q), .clk(R3_DIN), .clr(RESET));  // open: carry
  assign Addr = R3_AOUT ? counter_5_q : 8'bz;  // Controlled_Buffer controlled_buffer_8
  assign Data = PC_DOUT ? counter_1_q : 8'bz;  // Controlled_Buffer controlled_buffer_9
  assign Addr = PC_AOUT ? counter_1_q : 8'bz;  // Controlled_Buffer controlled_buffer_10
  assign Data = R0_DOUT ? counter_6_q : 8'bz;  // Controlled_Buffer controlled_buffer_11
  Counter counter_6 (.load(R_LD), .D(Data), .count(R_CT), .Q(counter_6_q), .clk(SP_DIN), .clr(RESET));  // open: carry
  assign Addr = SP_AOUT ? counter_6_q : 8'bz;  // Controlled_Buffer controlled_buffer_12
  RAM #(.bus("asynch")) ram_1 (.addr(Addr), .data(ram_1_data), .sel(not_2_out), .ld(not_3_out), .clr(1'b0));
  not not_3 (not_3_out, or_3_out);
  and and_1 (PCLDR, PC_LD, multiplexer_1_out);
  Multiplexer #(.select(3), .disabled(0), .enable("false")) multiplexer_1 (
    .in0(1'b1), .in1(DZ), .in2(DNZ), .in3(GT), .in4(LT), .in5(EQ), .in6(ANZ), .in7(AZ),
    .out(multiplexer_1_out), .sel({COND2, COND1, COND0}));
  // Probe on {COND2, COND1, COND0}
  or or_1 (DNZ, Data[0], Data[1], Data[2], Data[3], Data[4], Data[5], Data[6], Data[7]);
  assign Data = MEM_OUT ? ram_1_data : 8'bz;  // Controlled_Buffer controlled_buffer_13
  or or_2 (or_2_out, MEM_IN, LOAD);
  assign ram_1_data = or_2_out ? Data : 8'bz;  // Controlled_Buffer controlled_buffer_14
  or or_3 (or_3_out, MEM_WR, LD_WR);
  not not_4 (DZ, DNZ);
  Register Branch_Register (.D(Data), .en(RUN), .Q(BData), .clk(LD_BR), .clr(RESET));
  Clock clk (.out(clk_out));
  Counter #(.width(5), .max('h1f)) uCode_PC (
    .load(1'b0), .count(RUN), .Q(uCode_PC_q), .clk(clk_out), .clr(or_4_out));  // open: D, carry
  or or_4 (or_4_out, RESET, RST_UC);
  assign controlled_buffer_15_out = AC_IN ? Data : 8'bz;  // Controlled_Buffer controlled_buffer_15
  not not_5 (AZ, ANZ);
  not not_6 (R_LD, rom_1_data[23]);
  // Probe on uCode_PC_q
  Clock LD_CLK (.out(LD_CLK_out));
  Register register_1 (.D(controlled_buffer_15_out), .en(RUN), .Q(register_1_q), .clk(AC_WR), .clr(RESET));
  or or_5 (ANZ, register_1_q[0], register_1_q[1], register_1_q[2], register_1_q[3], register_1_q[4], register_1_q[5], register_1_q[6], register_1_q[7]);
  Register Inst_Reg (.D(Data), .en(RUN), .Q(Inst_Reg_q), .clk(LD_INS), .clr(RESET));
  Counter #(.width(10), .max('h3ff)) counter_7 (
    .Q(counter_7_q), .clk(LD_CLK_out), .clr(or_6_out));  // open: load, D, count, carry
  or or_6 (or_6_out, RESET, not_7_out);
  not not_7 (not_7_out, LOAD);
  assign Data = AC_OUT ? register_1_q : 8'bz;  // Controlled_Buffer controlled_buffer_16
  ROM #(.addrWidth(13), .dataWidth(32)) rom_1 (
    .addr({Inst_Reg_q, uCode_PC_q}),
    .data({RST_UC, LD_INS, SP_AOUT, SP_DIN, COND2, COND1, COND0, R_CT, rom_1_data[23], LD_BR, PC_INC, PC_LD, PC_AOUT, MEM_RD, MEM_WR, MEM_OUT, MEM_IN, IOW, IOR, IOADDR, R3_DIN, R3_AOUT, R3_DOUT, R2_DIN, R2_AOUT, R2_DOUT, R1_DIN, R1_AOUT, R1_DOUT, R0_DIN, R0_AOUT, R0_DOUT}),
    .sel(1'b1));
  ROM #(.addrWidth(13)) rom_2 (
    .addr({Inst_Reg_q, uCode_PC_q}), .data({rom_2_data[7], AC_WR, AC_OUT, AC_IN, ALUSEL}), .sel(1'b1));
  not not_8 (not_8_out, counter_7_q[0]);
  assign Addr = LOAD ? counter_7_q[9:2] : 8'bz;  // Controlled_Buffer controlled_buffer_17
  Register IO_Address (.D(Data), .en(RUN), .Q(IO_Address_q), .clk(IOADDR), .clr(RESET));
  and and_2 (LD_WR, not_8_out, counter_7_q[1], LOAD);
  Comparator comparator_1 (.a(Data), .b(register_1_q), .gt(GT), .eq(EQ), .lt(LT));
  Adder adder_1 (.a(Data), .b(register_1_q), .out(adder_1_out));  // open: cin, cout
  assign not_9_out = ~register_1_q;  // NOT_Gate not_9, 8 bits wide
  assign xor_1_out = Data ^ register_1_q;  // XOR_Gate xor_1, 8 bits wide
  assign or_7_out = Data | register_1_q;  // OR_Gate or_7, 8 bits wide
  assign and_3_out = Data & register_1_q;  // AND_Gate and_3, 8 bits wide
  Hex_Digit_Display hex_digit_display_1 (.value(register_2_q_2));  // open: dp
  Register register_2 (.D(Data), .en(IO1), .Q({register_2_q_2, register_2_q}), .clk(IOW), .clr(RESET));
  ROM rom_3 (.addr(Addr), .data(rom_3_data), .sel(LOAD));
  assign Data = LOAD ? rom_3_data : 8'bz;  // Controlled_Buffer controlled_buffer_18
  Decoder #(.select(3), .enable("false")) decoder_1 (
    .out1(IO1), .out2(IO2), .out3(IO3), .out4(IO4), .out5(IO5), .out6(IO6), .out7(IO7),
    .sel(IO_Address_q[2:0]));  // open: out0
  Pull_Resistor #(.pull(1)) pull_resistor_1 (.node(RESET));
  Hex_Digit_Display hex_digit_display_2 (.value(register_2_q));  // open: dp
  Multiplexer #(.select(4), .width(8), .enable("false")) multiplexer_2 (
    .in11(adder_1_out), .in12(not_9_out), .in13(xor_1_out), .in14(or_7_out), .in15(and_3_out),
    .out(controlled_buffer_15_out), .sel(ALUSEL));  // open: in0, in1, in2, in3, in4, in5, in6, in7, in8, in9, in10
  // Probe on ALUSEL

  // Notes on the sheet:
  //   PC
  //   SP
  //   RAM
  //   BRANCH SELECTOR
  //   DATA BUS CONDITIONS
  //   REGISTER FILE
  //   contents of rom_1 (hex, n*v repeats v):
  //   0 d0000 400d0000 200000 80000000 27*0 d0000 400d0000 200000 1 21 80000000 26*0 d0000 400d0000 200000
  //   1 101 80000000 26*0 d0000 400d0000 200000 1 801 80000000 26*0 d0000 400d0000 200000 8 c 80000000
  //   58*0 d0000 400d0000 200000 8 108 80000000 26*0 d0000 400d0000 200000 8 808 80000000 26*0 d0000
  //   400d0000 200000 40 44 80000000 26*0 d0000 400d0000 200000 40 60 80000000 58*0 d0000 400d0000 200000
  //   40 840 80000000 26*0 d0000 400d0000 200000 200 204 80000000 26*0 d0000 400d0000 200000 200 220
  //   80000000 26*0 d0000 400d0000 200000 200 300 80000000 90*0 d0000 400d0000 200000 10002 10022 80000000
  //   26*0 d0000 400d0000 200000 10002 10102 80000000 26*0 d0000 400d0000 200000 10002 10802 80000000 26*0
  //   d0000 400d0000 200000 10010 10014 80000000 58*0 d0000 400d0000 200000 10010 10110 80000000 26*0
  //   d0000 400d0000 200000 10010 10810 80000000 26*0 d0000 400d0000 200000 10080 10084 80000000 26*0
  //   d0000 400d0000 200000 10080 100a0 80000000 58*0 d0000 400d0000 200000 10080 10880 80000000 26*0
  //   d0000 400d0000 200000 10400 10404 80000000 26*0 d0000 400d0000 200000 10400 10420 80000000 26*0
  //   d0000 400d0000 200000 10400 10500 80000000 90*0 d0000 400d0000 200000 8011 28011 80000000 26*0 d0000
  //   400d0000 200000 8081 28081 80000000 26*0 d0000 400d0000 200000 8401 28401 80000000 26*0 d0000
  //   400d0000 200000 800a 2800a 80000000 58*0 d0000 400d0000 200000 8088 28088 80000000 26*0 d0000
  //   400d0000 200000 8408 28408 80000000 26*0 d0000 400d0000 200000 8042 28042 80000000 26*0 d0000
  //   400d0000 200000 8050 28050 80000000 58*0 d0000 400d0000 200000 8440 28440 80000000 26*0 d0000
  //   400d0000 200000 8202 28202 80000000 26*0 d0000 400d0000 200000 8210 28210 80000000 26*0 d0000
  //   400d0000 200000 8280 28280 80000000 570*0 d0000 400d0000 200000 90000 90004 200000 80000000 25*0
  //   d0000 400d0000 200000 90000 90020 200000 80000000 25*0 d0000 400d0000 200000 90000 90100 200000
  //   80000000 25*0 d0000 400d0000 200000 90000 90800 200000 80000000 1817*0 d0000 400d0000 200000 d0000
  //   d1000 50002 54002 200000 80000000 23*0 d0000 400d0000 200000 d0000 d1000 50010 54010 200000 80000000
  //   23*0 d0000 400d0000 200000 d0000 d1000 50080 54080 200000 80000000 23*0 d0000 400d0000 200000 d0000
  //   d1000 50400 54400 200000 80000000 23*0 d0000 400d0000 200000 d0000 4d0000 100000 200000 80000000
  //   2040*0 d0000 400d0000 200000 1800000 1800004 80000000 26*0 d0000 400d0000 200000 1800000 1800020
  //   80000000 26*0 d0000 400d0000 200000 1800000 1800100 80000000 26*0 d0000 400d0000 200000 1800000
  //   1800800 80000000 26*0 d0000 400d0000 200000 1800000 1800004 80000000 26*0 d0000 400d0000 200000
  //   1800000 1800020 80000000 26*0 d0000 400d0000 200000 1800000 1800100 80000000 26*0 d0000 400d0000
  //   200000 1800000 1800800 80000000 26*0 d0000 400d0000 200000 d0000 4d0000 2000001 2100001 200000
  //   80000000 23*0 d0000 400d0000 200000 d0000 4d0000 2000008 2100008 200000 80000000 23*0 d0000 400d0000
  //   200000 d0000 4d0000 2000040 2100040 200000 80000000 23*0 d0000 400d0000 200000 d0000 4d0000 2000200
  //   2100200 200000 80000000 23*0 d0000 400d0000 200000 d0000 4d0000 4000001 4100001 200000 80000000 23*0
  //   d0000 400d0000 200000 d0000 4d0000 4000008 4100008 200000 80000000 23*0 d0000 400d0000 200000 d0000
  //   4d0000 4000040 4100040 200000 80000000 23*0 d0000 400d0000 200000 d0000 4d0000 4000200 4100200
  //   200000 80000000 23*0 d0000 400d0000 200000 1 1 80000000 26*0 d0000 400d0000 200000 8 8 80000000 26*0
  //   d0000 400d0000 200000 40 40 80000000 26*0 d0000 400d0000 200000 200 200 80000000 26*0 d0000 400d0000
  //   200000 0 4 80000000 26*0 d0000 400d0000 200000 0 20 80000000 26*0 d0000 400d0000 200000 0 100
  //   80000000 26*0 d0000 400d0000 200000 0 800 80000000 26*0 d0000 400d0000 200000 1 1 1 80000000 25*0
  //   d0000 400d0000 200000 8 8 8 80000000 25*0 d0000 400d0000 200000 40 40 40 80000000 25*0 d0000
  //   400d0000 200000 200 200 200 80000000
  //   contents of rom_2 (hex, n*v repeats v):
  //   6659*0 10 50 30*0 10 50 30*0 10 50 30*0 10 50 30*0 20 20 30*0 20 20 30*0 20 20 30*0 20 20 31*0 b 4b
  //   30*0 b 4b 30*0 b 4b 30*0 b 4b
  //   RAM LOADER
  //   contents of rom_3 (hex, n*v repeats v):
  //   40 54 43 2 42 11 1 26 7e 1 d0 db d4 c8 0 80 6
  //   CONTROL
endmodule
