// Logisim project test8.circ as structural Verilog: 1 circuit, main circuit Register File
module Register_File (
  input  RESET,
  input  RUN,
  input  LOAD,
  input  INT
);

  wire AC_IN, AC_OUT, AC_WR, and_2_out, and_3_out, clk_out, COND0, COND1, COND2, DNZ, DO_INT, DZ, EQ, Fault,
       GT, In_Int_qn, INT_EN, INT_END, INT_JMP, INT_START, IO1, IO2, IO3, IO4, IO5, IO6, IO7, IOADDR, IOR,
       IOW, LD_BR, LD_CLK_out, LD_INS, LD_WR, LOFF, LON, LT, MEM_IN, MEM_OUT, MEM_WR, multiplexer_1_out,
       not_1_out, not_2_out, not_3_out, not_5_out, not_6_out, not_9_out, not_10_out, or_1_out, or_2_out,
       or_4_out, or_5_out, or_7_out, PC_AOUT, PC_DOUT, PC_INC, PC_LD, PCLDR, Pending_q, R0_AOUT, R0_DIN,
       R0_DOUT, R1_AOUT, R1_DIN, R1_DOUT, R2_AOUT, R2_DIN, R2_DOUT, R3_AOUT, R3_DIN, R3_DOUT, R_CT, R_LD,
       RST_UC, s_r_ff_1_q, SP_AOUT, SP_DIN;
  wire [3:0] ALU_SEL, register_2_q, register_2_q_2, register_3_q, register_3_q_2;
  wire [4:0] uCode_PC_q;
  wire [7:0] adder_1_out, Addr, and_6_out, BData, controlled_buffer_15_out, controlled_buffer_17_out,
       counter_1_q, counter_2_q, counter_3_q, counter_4_q, counter_5_q, counter_6_q, Data, Inst_Reg_q,
       IO_Address_q, not_8_out, or_6_out, ram_1_data, register_1_q, rom_3_data, xor_1_out;
  wire [9:0] counter_7_q;
  wire [12:10] rom_2_data;
  wire [23:23] rom_1_data;

  Counter counter_1 (
    .load(PCLDR), .D(BData), .count(not_1_out), .Q(counter_1_q), .clk(PC_INC), .clr(RESET));  // open: carry
  not not_1 (not_1_out, PCLDR);
  not not_2 (not_2_out, 1'b0);
  assign Data = R0_DOUT ? counter_2_q : 8'bz;  // Controlled_Buffer controlled_buffer_1
  Counter counter_2 (.load(R_LD), .D(Data), .count(R_CT), .Q(counter_2_q), .clk(R0_DIN), .clr(RESET));  // open: carry
  assign Addr = R0_AOUT ? counter_2_q : 8'bz;  // Controlled_Buffer controlled_buffer_2
  assign Data = R1_DOUT ? counter_3_q : 8'bz;  // Controlled_Buffer controlled_buffer_3
  Counter counter_3 (.load(R_LD), .D(Data), .count(R_CT), .Q(counter_3_q), .clk(R1_DIN), .clr(RESET));  // open: carry
  assign Addr = R1_AOUT ? counter_3_q : 8'bz;  // Controlled_Buffer controlled_buffer_4
  assign Data = R2_DOUT ? counter_4_q : 8'bz;  // Controlled_Buffer controlled_buffer_5
  Counter counter_4 (.load(R_LD), .D(Data), .count(R_CT), .Q(counter_4_q), .clk(R2_DIN), .clr(RESET));  // open: carry
  assign Addr = R2_AOUT ? counter_4_q : 8'bz;  // Controlled_Buffer controlled_buffer_6
  assign Data = R3_DOUT ? counter_5_q : 8'bz;  // Controlled_Buffer controlled_buffer_7
  Counter counter_5 (.load(R_LD), .D(Data), .count(R_CT), .Q(counter_5_q), .clk(R3_DIN), .clr(RESET));  // open: carry
  assign Addr = R3_AOUT ? counter_5_q : 8'bz;  // Controlled_Buffer controlled_buffer_8
  assign Data = PC_DOUT ? counter_1_q : 8'bz;  // Controlled_Buffer controlled_buffer_9
  assign Addr = PC_AOUT ? counter_1_q : 8'bz;  // Controlled_Buffer controlled_buffer_10
  assign Addr = SP_AOUT ? counter_6_q : 8'bz;  // Controlled_Buffer controlled_buffer_11
  Counter counter_6 (.load(R_LD), .D(Data), .count(R_CT), .Q(counter_6_q), .clk(SP_DIN), .clr(RESET));  // open: carry
  RAM #(.bus("asynch")) ram_1 (.addr(Addr), .data(ram_1_data), .sel(not_2_out), .ld(not_3_out), .clr(1'b0));
  assign ram_1_data = or_2_out ? Data : 8'bz;  // Controlled_Buffer controlled_buffer_12
  not not_3 (not_3_out, or_1_out);
  or or_1 (or_1_out, MEM_WR, LD_WR);
  and and_1 (PCLDR, PC_LD, multiplexer_1_out);
  Multiplexer #(.select(3), .disabled(0), .enable("false")) multiplexer_1 (
    .in0(1'b1), .in1(DZ), .in2(DNZ), .in3(GT), .in4(LT), .in5(EQ), .out(multiplexer_1_out),
    .sel({COND2, COND1, COND0}));  // open: in6, in7
  assign Data = MEM_OUT ? ram_1_data : 8'bz;  // Controlled_Buffer controlled_buffer_13
  or or_2 (or_2_out, MEM_IN, LOAD);
  or or_3 (DNZ, Data[0], Data[1], Data[2], Data[3], Data[4], Data[5], Data[6], Data[7]);
  assign Addr = INT_JMP ? {8{1'b1}} : 8'bz;  // Controlled_Buffer controlled_buffer_14
  Register Branch_Register (.D(Data), .en(RUN), .Q(BData), .clk(LD_BR), .clr(RESET));
  not not_4 (DZ, DNZ);
  Clock clk (.out(clk_out));
  not not_5 (not_5_out, Fault);
  Counter #(.width(5), .max('h1f)) uCode_PC (
    .load(1'b0), .count(RUN), .Q(uCode_PC_q), .clk(and_2_out), .clr(or_4_out));  // open: D, carry
  and and_2 (and_2_out, clk_out, not_5_out);
  or or_4 (or_4_out, RESET, RST_UC);
  not not_6 (not_6_out, DO_INT);
  assign controlled_buffer_15_out = DO_INT ? {8{1'b1}} : 8'bz;  // Controlled_Buffer controlled_buffer_15
  not not_7 (R_LD, rom_1_data[23]);
  assign controlled_buffer_15_out = not_6_out ? Data : 8'bz;  // Controlled_Buffer controlled_buffer_16
  and and_3 (and_3_out, INT, s_r_ff_1_q);
  S_R_Flip_Flop s_r_ff_1 (.Q(s_r_ff_1_q), .preset(INT_EN), .reset(RESET));  // open: S, clk, R, Qn, en
  Register Inst_Reg (.D(controlled_buffer_15_out), .en(RUN), .Q(Inst_Reg_q), .clk(LD_INS), .clr(RESET));
  S_R_Flip_Flop Pending (.Q(Pending_q), .preset(and_3_out), .reset(or_5_out));  // open: S, clk, R, Qn, en
  assign controlled_buffer_17_out = AC_IN ? Data : 8'bz;  // Controlled_Buffer controlled_buffer_17
  and and_4 (Fault, R0_DOUT, R0_AOUT, R0_DIN, R1_DOUT, R1_AOUT, R1_DIN);
  ROM #(.addrWidth(13), .dataWidth(32)) rom_1 (
    .addr({Inst_Reg_q, uCode_PC_q}),
    .data({RST_UC, LD_INS, SP_AOUT, SP_DIN, COND2, COND1, COND0, R_CT, rom_1_data[23], LD_BR, PC_INC, PC_LD, PC_AOUT, PC_DOUT, MEM_WR, MEM_OUT, MEM_IN, IOW, IOR, IOADDR, R3_DIN, R3_AOUT, R3_DOUT, R2_DIN, R2_AOUT, R2_DOUT, R1_DIN, R1_AOUT, R1_DOUT, R0_DIN, R0_AOUT, R0_DOUT}),
    .sel(1'b1));
  ROM #(.addrWidth(13), .dataWidth(16)) rom_2 (
    .addr({Inst_Reg_q, uCode_PC_q}),
    .data({LOFF, LON, INT_JMP, rom_2_data, INT_EN, INT_END, INT_START, AC_WR, AC_OUT, AC_IN, ALU_SEL}),
    .sel(1'b1));
  S_R_Flip_Flop In_Int (.Qn(In_Int_qn), .preset(INT_START), .reset(or_5_out));  // open: S, clk, R, Q, en
  and and_5 (DO_INT, Pending_q, In_Int_qn);
  or or_5 (or_5_out, INT_END, RESET);
  Register register_1 (.D(controlled_buffer_17_out), .en(RUN), .Q(register_1_q), .clk(AC_WR), .clr(RESET));
  assign Data = AC_OUT ? register_1_q : 8'bz;  // Controlled_Buffer controlled_buffer_18
  Hex_Digit_Display hex_digit_display_1 (.value(register_2_q_2));  // open: dp
  Register register_2 (.D(Data), .en(IO1), .Q({register_2_q_2, register_2_q}), .clk(IOW), .clr(RESET));
  Hex_Digit_Display hex_digit_display_2 (.value(register_2_q));  // open: dp
  Comparator comparator_1 (.a(Data), .b(register_1_q), .gt(GT), .eq(EQ), .lt(LT));
  Adder adder_1 (.a(Data), .b(register_1_q), .out(adder_1_out));  // open: cin, cout
  assign not_8_out = ~register_1_q;  // NOT_Gate not_8, 8 bits wide
  assign xor_1_out = Data ^ register_1_q;  // XOR_Gate xor_1, 8 bits wide
  assign or_6_out = Data | register_1_q;  // OR_Gate or_6, 8 bits wide
  assign and_6_out = Data & register_1_q;  // AND_Gate and_6, 8 bits wide
  Clock LD_CLK (.out(LD_CLK_out));
  or or_7 (or_7_out, RESET, not_9_out);
  S_R_Flip_Flop s_r_ff_2 (.preset(LON), .reset(LOFF));  // open: S, clk, R, Q, Qn, en
  Hex_Digit_Display hex_digit_display_3 (.value(register_3_q_2));  // open: dp
  Register register_3 (.D(Data), .en(IO2), .Q({register_3_q_2, register_3_q}), .clk(IOW), .clr(RESET));
  // Probe on Data
  // Probe on Addr
  // Probe on BData
  // Probe on ALU_SEL
  // Probe on {COND2, COND1, COND0}
  // Probe on Fault
  Multiplexer #(.select(4), .width(8), .enable("false")) multiplexer_2 (
    .in11(adder_1_out), .in12(not_8_out), .in13(xor_1_out), .in14(or_6_out), .in15(and_6_out),
    .out(controlled_buffer_17_out), .sel(ALU_SEL));  // open: in0, in1, in2, in3, in4, in5, in6, in7, in8, in9, in10
  Counter #(.width(10), .max('h3ff)) counter_7 (
    .Q(counter_7_q), .clk(LD_CLK_out), .clr(or_7_out));  // open: load, D, count, carry
  not not_9 (not_9_out, LOAD);
  Hex_Digit_Display hex_digit_display_4 (.value(register_3_q));  // open: dp
  not not_10 (not_10_out, counter_7_q[0]);
  assign Addr = LOAD ? counter_7_q[9:2] : 8'bz;  // Controlled_Buffer controlled_buffer_19
  Register IO_Address (.D(Data), .en(RUN), .Q(IO_Address_q), .clk(IOADDR), .clr(RESET));
  and and_7 (LD_WR, not_10_out, counter_7_q[1], LOAD);
  Decoder #(.select(3), .enable("false")) decoder_1 (
    .out1(IO1), .out2(IO2), .out3(IO3), .out4(IO4), .out5(IO5), .out6(IO6), .out7(IO7),
    .sel(IO_Address_q[2:0]));  // open: out0
  assign Data = LOAD ? rom_3_data : 8'bz;  // Controlled_Buffer controlled_buffer_20
  ROM rom_3 (.addr(Addr), .data(rom_3_data), .sel(LOAD));

  // Other names for the same wires on the sheet: COND_SEL[2:0] = {COND2, COND1, COND0}

  // Notes on the sheet:
  //   PC
  //   SP
  //   RAM
  //   REGISTER FILE
  //   BRANCH SELECTOR
  //   DATA BUS CONDITIONS
  //   INTERRUPT MGMT
  //   INSTRUCTION FAULT
  //   contents of rom_1 (hex, n*v repeats v):
  //   0 90000 40090000 200000 80000000 27*ff 0 90000 40090000 200000 1 21 80000000 25*ff 0 90000 40090000
  //   200000 1 101 80000000 25*ff 0 90000 40090000 200000 1 801 80000000 25*ff 0 90000 40090000 200000 8 c
  //   80000000 57*ff 0 90000 40090000 200000 8 108 80000000 25*ff 0 90000 40090000 200000 8 808 80000000
  //   25*ff 0 90000 40090000 200000 40 44 80000000 25*ff 0 90000 40090000 200000 40 60 80000000 57*ff 0
  //   90000 40090000 200000 40 840 80000000 25*ff 0 90000 40090000 200000 200 204 80000000 25*ff 0 90000
  //   40090000 200000 200 220 80000000 25*ff 0 90000 40090000 200000 200 300 80000000 89*ff 0 90000
  //   40090000 200000 10002 10022 80000000 25*ff 0 90000 40090000 200000 10002 10102 80000000 25*ff 0
  //   90000 40090000 200000 10002 10802 80000000 25*ff 0 90000 40090000 200000 10010 10014 80000000 57*ff
  //   0 90000 40090000 200000 10010 10110 80000000 25*ff 0 90000 40090000 200000 10010 10810 80000000
  //   25*ff 0 90000 40090000 200000 10080 10084 80000000 25*ff 0 90000 40090000 200000 10080 100a0
  //   80000000 57*ff 0 90000 40090000 200000 10080 10880 80000000 25*ff 0 90000 40090000 200000 10400
  //   10404 80000000 25*ff 0 90000 40090000 200000 10400 10420 80000000 25*ff 0 90000 40090000 200000
  //   10400 10500 80000000 89*ff 0 90000 40090000 200000 8011 28011 80000000 25*ff 0 90000 40090000 200000
  //   8081 28081 80000000 25*ff 0 90000 40090000 200000 8401 28401 80000000 25*ff 0 90000 40090000 200000
  //   800a 2800a 80000000 57*ff 0 90000 40090000 200000 8088 28088 80000000 25*ff 0 90000 40090000 200000
  //   8408 28408 80000000 25*ff 0 90000 40090000 200000 8042 28042 80000000 25*ff 0 90000 40090000 200000
  //   8050 28050 80000000 57*ff 0 90000 40090000 200000 8440 28440 80000000 25*ff 0 90000 40090000 200000
  //   8202 28202 80000000 25*ff 0 90000 40090000 200000 8210 28210 80000000 25*ff 0 90000 40090000 200000
  //   8280 28280 80000000 569*ff 0 90000 40090000 200000 90000 90004 200000 80000000 24*ff 0 90000
  //   40090000 200000 90000 90020 200000 80000000 24*ff 0 90000 40090000 200000 90000 90100 200000
  //   80000000 24*ff 0 90000 40090000 200000 90000 90800 200000 80000000 152*ff 0 90000 40090000 200000
  //   90000 490000 2000001 2100001 200000 80000000 22*ff 0 90000 40090000 200000 90000 490000 2000008
  //   2100008 200000 80000000 22*ff 0 90000 40090000 200000 90000 490000 2000040 2100040 200000 80000000
  //   22*ff 0 90000 40090000 200000 90000 490000 2000200 2100200 200000 80000000 22*ff 0 90000 40090000
  //   200000 90000 490000 4000001 4100001 200000 80000000 22*ff 0 90000 40090000 200000 90000 490000
  //   4000008 4100008 200000 80000000 22*ff 0 90000 40090000 200000 90000 490000 4000040 4100040 200000
  //   80000000 22*ff 0 90000 40090000 200000 90000 490000 4000200 4100200 200000 80000000 1430*ff 0 90000
  //   40090000 200000 90000 91000 10002 14002 200000 80000000 22*ff 0 90000 40090000 200000 90000 91000
  //   10010 14010 200000 80000000 22*ff 0 90000 40090000 200000 90000 91000 10080 14080 200000 80000000
  //   22*ff 0 90000 40090000 200000 90000 91000 10400 14400 200000 80000000 22*ff 0 90000 40090000 200000
  //   90000 490000 100000 300000 80000000 23*ff 0 90000 40090000 200000 90000 10090000 200000 80000000
  //   984*ff 0 90000 40090000 200000 0 80000000 26*ff 0 90000 40090000 200000 0 80000000 26*ff 0 90000
  //   40090000 200000 1800000 11800000 20010000 20410000 100000 300000 80000000 21*ff 0 90000 40090000
  //   200000 0 80000000 26*ff 0 90000 40090000 200000 1800000 11800000 20010000 20410000 100000 300000
  //   80000000 885*ff 0 90000 40090000 200000 1800000 1800004 80000000 25*ff 0 90000 40090000 200000
  //   1800000 1800020 80000000 25*ff 0 90000 40090000 200000 1800000 1800100 80000000 25*ff 0 90000
  //   40090000 200000 1800000 1800800 80000000 25*ff 0 90000 40090000 200000 1000000 1000004 80000000
  //   25*ff 0 90000 40090000 200000 1000000 1000020 80000000 25*ff 0 90000 40090000 200000 1000000 1000100
  //   80000000 25*ff 0 90000 40090000 200000 1000000 1000800 80000000 281*ff 0 90000 40090000 200000 1 1
  //   80000000 25*ff 0 90000 40090000 200000 8 8 80000000 25*ff 0 90000 40090000 200000 40 40 80000000
  //   25*ff 0 90000 40090000 200000 200 200 80000000 25*ff 0 90000 40090000 200000 0 4 80000000 25*ff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
  //   contents of rom_2 (hex, n*v repeats v):
  //   5124*0 8000 31*0 4000 63*0 200 36*0 100 1402*0 10 50 30*0 10 50 30*0 10 50 30*0 10 50 30*0 20 20
  //   30*0 20 20 30*0 20 20 30*0 20 20 31*0 b 4b 30*0 b 4b 30*0 b 4b 30*0 b 4b 1149*0 80 4*0 2000 2000
  //   ROM1
  //   ROM2
  //   OUT 1
  //   CONTROL
  //   ALU
  //   LED
  //   PROBES
  //   OUT 2
  //   IO DECODER
  //   RAM LOADER
  //   contents of rom_3 (hex, n*v repeats v):
  //   81 fe a3 40 54 41 1c 42 2 43 16 fb 21 7d 1 d0 da d4 48 3 80 b a1 a0 a2 7d 2 a4 227*0 19
endmodule
